# Fritzing sketch Diagram Sketch (saved by Fritzing 0.9.2b)
breadboards: 1

parts:
  DS1 = DS18B20 1-Wire Temperature Sensor Probe Cable
  R1 = Resistor [tolerance=±5% resistance=220 package=THT]
  Part1 = Arduino Uno (Rev3)
  M1 = ph-4502c [package=THT]

nets:
  GND: DS1.GND, Part1.GND, M1.pin5
  VDD: DS1.VDD, R1.Pin_1, Part1.5V, M1.pin6
  N1: DS1.shield, R1.Pin_0, Part1.A0
  N2: Part1.A1, M1.pin3

custom parts:
  ph-4502c: ph-4502c PH Meter.
